// Logisim project MipsSingleCycleCPU.circ as structural Verilog: 4 circuits, main circuit main
module main (
  input  in_1
);

  wire alu_1_iszero, IsImmediate, IsJump, RegWrite;
  wire [1:0] AluCntrl;
  wire [4:0] DestReg;
  wire [5:0] funct, OpCode;
  wire [15:6] Immediate;
  wire [25:16] JumpAddr;
  wire [27:0] PC_PLUS_4;
  wire [31:0] AluResult, multiplexer_1_out, multiplexer_3_out, register_1_q, registerfile_1_avalue,
       registerfile_1_bvalue, SEImmediate;
  wire [31:28] PC_ADDRESS_TO_JUMP_TO;

  Adder #(.width(32)) adder_1 (
    .a(32'h4), .b(register_1_q), .out({PC_ADDRESS_TO_JUMP_TO, PC_PLUS_4}));  // open: cin, cout
  Multiplexer #(.enable("false"), .width(32)) multiplexer_1 (
    .in0({PC_ADDRESS_TO_JUMP_TO, PC_PLUS_4}),
    .in1({PC_ADDRESS_TO_JUMP_TO, JumpAddr, Immediate, funct, 2'b00}), .out(multiplexer_1_out), .sel(IsJump));
  Register #(.width(32)) register_1 (.D(multiplexer_1_out), .clk(in_1), .Q(register_1_q));  // open: en, clr
  ROM #(.dataWidth(32)) rom_1 (.data({OpCode, JumpAddr, Immediate, funct}));  // open: addr
  assign SEImmediate = {{16{Immediate[15]}}, {Immediate, funct}};  // Bit_Extender bit_extender_1
  Multiplexer #(.enable("false"), .width(5)) multiplexer_2 (
    .in0(Immediate[15:11]), .in1(JumpAddr[20:16]), .out(DestReg), .sel(IsImmediate));
  ControlSignals controlsignals_1 (
    .OpCodeIn(OpCode), .FunctIn(funct), .IsJumpOut(IsJump), .IsImmediateOut(IsImmediate), .RegWrite(RegWrite));
  RegisterFile registerfile_1 (
    .RegA(JumpAddr[25:21]), .RegB(JumpAddr[20:16]), .RegDest(DestReg), .DestValue(AluResult),
    .WriteTheValue(RegWrite), .AValue(registerfile_1_avalue), .BValue(registerfile_1_bvalue));
  Multiplexer #(.enable("false"), .width(32)) multiplexer_3 (
    .in0(registerfile_1_bvalue), .in1(SEImmediate), .out(multiplexer_3_out), .sel(IsImmediate));
  ALU alu_1 (
    .ALU_OPIn(AluCntrl), .AIn(registerfile_1_avalue), .Bin(multiplexer_3_out), .IsZero(alu_1_iszero),
    .AluResultOut(AluResult));
  RAM #(.dataWidth(32)) ram_1 ();  // open: addr, we, oe, clk, din, dout

  // Other names for the same wires on the sheet: Immediate[5:0] = funct; JumpAddr[15:0] = {Immediate, funct};
  //   PC_ADDRESS_TO_JUMP_TO[27:2] = {JumpAddr, Immediate, funct}; shamt[4:0] = Immediate[10:6];
  //   rd[4:0] = Immediate[15:11]; rt[4:0] = JumpAddr[20:16]; rs[4:0] = JumpAddr[25:21]; clk = in_1;
  //   PC_PLUS_4[31:28] = PC_ADDRESS_TO_JUMP_TO

  // Notes on the sheet:
  //   000000000010
  //   111111111110
endmodule

module RegisterFile (
  input  [4:0] RegA,
  input  [4:0] RegB,
  input  [4:0] RegDest,
  input  [31:0] DestValue,
  input  WriteTheValue,
  output [31:0] AValue,
  output [31:0] BValue
);
endmodule

module ALU (
  input  [1:0] ALU_OPIn,
  input  [31:0] AIn,
  input  [31:0] Bin,
  output IsZero,
  output [31:0] AluResultOut
);

  wire [31:0] adder_1_out, and_1_out, or_1_out, subtractor_1_out;

  Adder #(.width(32)) adder_1 (.a(AIn), .b(Bin), .out(adder_1_out));  // open: cin, cout
  Subtractor #(.width(32)) subtractor_1 (.a(AIn), .b(Bin), .out(subtractor_1_out));  // open: bin, bout
  assign and_1_out = AIn & Bin;  // AND_Gate and_1, 32 bits wide
  assign or_1_out = AIn | Bin;  // OR_Gate or_1, 32 bits wide
  Multiplexer #(.enable("false"), .select(2), .width(32)) multiplexer_1 (
    .in0(adder_1_out), .in1(subtractor_1_out), .in2(and_1_out), .in3(or_1_out), .out(AluResultOut),
    .sel(ALU_OPIn));
  Comparator #(.width(32)) comparator_1 (.a(AluResultOut), .b({32{1'b0}}), .eq(IsZero));  // open: gt, lt

  // Other names for the same wires on the sheet: A[31:0] = AIn; ALU_OP[1:0] = ALU_OPIn;
  //   AluResult[31:0] = AluResultOut; B[31:0] = Bin
endmodule

module ControlSignals (
  input  [5:0] OpCodeIn,
  input  [5:0] FunctIn,
  output IsJumpOut,
  output IsImmediateOut,
  output RegWrite
);

  wire comparator_2_eq;

  Comparator #(.width(6)) comparator_1 (.a(OpCodeIn), .b(6'b000010), .eq(IsJumpOut));  // open: gt, lt
  not not_1 (IsImmediateOut, comparator_2_eq);
  Comparator #(.width(6)) comparator_2 (.a(OpCodeIn), .b({6{1'b0}}), .eq(comparator_2_eq));  // open: gt, lt
  not not_2 (RegWrite, IsJumpOut);

  // Other names for the same wires on the sheet: IsJump = IsJumpOut; OpCode[5:0] = OpCodeIn
endmodule
